// Logisim project GeoRAM interfacing.circ as structural Verilog: 1 circuit, main circuit main
// LATCH1
module main (
  input  A0,
  input  nIO2,
  input  R_W,
  input  nIO1
);

  wire and_1_out, and_2_out, and_3_out, and_4_out, nand_1_out, nand_2_out, nand_3_out, nand_4_out, not_1_out,
       not_2_out, not_3_out, not_4_out, not_5_out, not_6_out, PHI2_out;

  Clock PHI2 (.out(PHI2_out));
  not not_1 (not_1_out, A0);
  not not_2 (not_2_out, not_1_out);
  not not_3 (not_3_out, nIO2);
  not not_4 (not_4_out, R_W);
  not not_5 (not_5_out, nIO1);
  and and_1 (and_1_out, PHI2_out, not_4_out);
  and and_2 (and_2_out, not_3_out, and_1_out);
  nand nand_1 (nand_1_out, and_1_out, not_5_out);
  nand nand_2 (nand_2_out, not_5_out, not_5_out);
  nand nand_3 (nand_3_out, not_3_out, not_3_out);
  and and_3 (and_3_out, not_2_out, and_2_out);
  and and_4 (and_4_out, and_2_out, not_1_out);
  nand nand_4 (nand_4_out, nand_2_out, nand_3_out);
  not not_6 (not_6_out, nand_4_out);

  // Notes on the sheet:
  //   A0 buffered
  //   /WE SRAM
  //   /CS SRAM
  //   LATCH2 @ $DFFF (74LS573)
  //   LATCH1 @ $DFFE  (74LS573)
  //   /OE bus transceiver (74LS245)
  //   DIR bus transceiver (74LS245)
endmodule
