// Logisim project digital-locker.circ as structural Verilog: 1 circuit, main circuit main
module main (
);

  wire and_1_out, and_2_out, button_1_out, button_2_out, button_3_out, button_4_out, clock_1_out,
       controlled_buffer_1_out, controlled_buffer_2_out, d_ff_1_q, d_ff_2_q, not_1_out, not_2_out, not_3_out,
       not_4_out, not_5_out;

  Button button_1 (.out(button_1_out));
  Button button_2 (.out(button_2_out));
  Button button_3 (.out(button_3_out));
  Button button_4 (.out(button_4_out));
  assign controlled_buffer_1_out = button_1_out ? 1'b0 : 1'bz;  // Controlled_Buffer controlled_buffer_1
  assign controlled_buffer_2_out = button_1_out ? 1'b0 : 1'bz;  // Controlled_Buffer controlled_buffer_2
  assign controlled_buffer_1_out = button_2_out ? 1'b0 : 1'bz;  // Controlled_Buffer controlled_buffer_3
  assign controlled_buffer_2_out = button_2_out ? 1'b1 : 1'bz;  // Controlled_Buffer controlled_buffer_4
  assign controlled_buffer_1_out = button_3_out ? 1'b1 : 1'bz;  // Controlled_Buffer controlled_buffer_5
  assign controlled_buffer_2_out = button_3_out ? 1'b0 : 1'bz;  // Controlled_Buffer controlled_buffer_6
  assign controlled_buffer_1_out = button_4_out ? 1'b1 : 1'bz;  // Controlled_Buffer controlled_buffer_7
  assign controlled_buffer_2_out = button_4_out ? 1'b1 : 1'bz;  // Controlled_Buffer controlled_buffer_8
  Clock clock_1 (.out(clock_1_out));
  not not_1 (not_1_out, clock_1_out);
  LED led_1 (.in(clock_1_out));
  LED led_2 (.in(not_1_out));
  not not_2 (not_2_out, controlled_buffer_1_out);
  not not_3 (not_3_out, controlled_buffer_2_out);
  not not_4 (not_4_out, d_ff_1_q);
  D_Flip_Flop d_ff_1 (.clk(clock_1_out), .D(and_1_out), .Q(d_ff_1_q));  // open: Qn, preset, en, reset
  not not_5 (not_5_out, d_ff_2_q);
  D_Flip_Flop d_ff_2 (.clk(clock_1_out), .D(and_2_out), .Q(d_ff_2_q));  // open: Qn, preset, en, reset
  and and_1 (and_1_out, controlled_buffer_1_out, not_3_out, not_4_out, not_5_out);
  and and_2 (and_2_out, not_2_out, controlled_buffer_2_out, d_ff_1_q, not_5_out);
  LED led_3 (.in(d_ff_2_q));

  // Notes on the sheet:
  //   00
  //   01
  //   10
  //   11
endmodule
