// Logisim project 4bitcounter.circ as structural Verilog: 1 circuit, main circuit main
module main (
  input  CLR,
  input  SET,
  input  D0,
  input  D1,
  input  D2,
  input  D3
);

  wire and_1_out, and_2_out, and_3_out, and_4_out, and_5_out, and_6_out, and_7_out, and_8_out, and_9_out,
       and_10_out, and_11_out, and_12_out, and_13_out, and_14_out, clock_1_out, d_ff_1_q, d_ff_1_qn,
       d_ff_2_q, d_ff_2_qn, d_ff_3_q, d_ff_3_qn, d_ff_4_q, d_ff_4_qn, not_1_out, not_2_out, or_1_out,
       or_2_out, or_3_out, or_4_out;

  not not_1 (not_1_out, CLR);
  not not_2 (not_2_out, SET);
  and and_1 (and_1_out, not_1_out, SET, D0);
  and and_2 (and_2_out, not_1_out, not_2_out, d_ff_1_qn);
  and and_3 (and_3_out, not_1_out, SET, D1);
  and and_4 (and_4_out, not_1_out, not_2_out, d_ff_2_qn, d_ff_1_q);
  and and_5 (and_5_out, not_1_out, not_2_out, d_ff_2_q, d_ff_1_qn);
  and and_6 (and_6_out, not_1_out, SET, D2);
  and and_7 (and_7_out, not_1_out, not_2_out, d_ff_3_q, d_ff_2_qn);
  and and_8 (and_8_out, not_1_out, not_2_out, d_ff_3_q, d_ff_1_qn);
  and and_9 (and_9_out, not_1_out, not_2_out, d_ff_3_qn, d_ff_2_q, d_ff_1_q);
  and and_10 (and_10_out, not_1_out, SET, D3);
  and and_11 (and_11_out, not_1_out, not_2_out, d_ff_4_q, d_ff_2_qn);
  and and_12 (and_12_out, not_1_out, not_2_out, d_ff_4_q, d_ff_1_qn);
  and and_13 (and_13_out, not_1_out, not_2_out, d_ff_4_q, d_ff_3_qn);
  and and_14 (and_14_out, not_1_out, not_2_out, d_ff_4_qn, d_ff_3_q, d_ff_2_q, d_ff_1_q);
  Clock clock_1 (.out(clock_1_out));
  or or_1 (or_1_out, and_1_out, and_2_out);
  or or_2 (or_2_out, and_3_out, and_4_out, and_5_out);
  or or_3 (or_3_out, and_6_out, and_7_out, and_8_out, and_9_out);
  or or_4 (or_4_out, and_10_out, and_11_out, and_12_out, and_13_out, and_14_out);
  D_Flip_Flop d_ff_1 (.D(or_1_out), .clk(clock_1_out), .Q(d_ff_1_q), .Qn(d_ff_1_qn), .preset(1'b0), .reset(1'b0));
  D_Flip_Flop d_ff_2 (.D(or_2_out), .clk(clock_1_out), .Q(d_ff_2_q), .Qn(d_ff_2_qn), .preset(1'b0), .reset(1'b0));
  D_Flip_Flop d_ff_3 (.D(or_3_out), .clk(clock_1_out), .Q(d_ff_3_q), .Qn(d_ff_3_qn), .preset(1'b0), .reset(1'b0));
  D_Flip_Flop d_ff_4 (.D(or_4_out), .clk(clock_1_out), .Q(d_ff_4_q), .Qn(d_ff_4_qn), .preset(1'b0), .reset(1'b0));
  LED led_1 (.in(d_ff_1_q));
  LED led_2 (.in(d_ff_2_q));
  LED led_3 (.in(d_ff_3_q));
  LED led_4 (.in(d_ff_4_q));
endmodule
