// Logisim project 6502_AY_3_891x.circ as structural Verilog: 1 circuit, main circuit main
module main (
  input  in_1,
  input  A0,
  input  nDEV_SELECT,
  input  nWR_RD
);

  wire and_1_out, and_2_out, and_3_out, and_4_out, d_ff_1_q, d_ff_2_q, nor_1_out, nor_2_out, nor_3_out,
       nor_4_out, not_1_out, not_2_out, not_3_out, not_4_out, not_5_out, not_6_out, not_7_out, or_1_out,
       PHI1_out, xor_1_out;

  Clock PHI1 (.out(PHI1_out));
  nor nor_1 (nor_1_out, PHI1_out, nDEV_SELECT);
  xor xor_1 (xor_1_out, nor_1_out, nWR_RD);
  D_Flip_Flop d_ff_1 (.D(A0), .clk(not_1_out), .Q(d_ff_1_q), .reset(in_1));  // open: Qn, preset
  not not_1 (not_1_out, xor_1_out);
  D_Flip_Flop d_ff_2 (.D(nDEV_SELECT), .clk(not_1_out), .Q(d_ff_2_q), .preset(in_1));  // open: Qn, reset
  not not_2 (not_2_out, d_ff_2_q);
  not not_3 (not_3_out, nWR_RD);
  and and_1 (and_1_out, d_ff_1_q, not_2_out);
  and and_2 (and_2_out, not_2_out, nWR_RD);
  not not_4 (not_4_out, nWR_RD);
  or or_1 (or_1_out, and_1_out, and_2_out);
  and and_3 (and_3_out, not_2_out, not_4_out);
  not not_5 (not_5_out, nWR_RD);
  LED WRITE (.in(not_5_out));
  LED READ (.in(nWR_RD));
  nor nor_2 (nor_2_out, and_3_out, or_1_out);
  nor nor_3 (nor_3_out, and_3_out, not_6_out);
  not not_6 (not_6_out, or_1_out);
  nor nor_4 (nor_4_out, not_7_out, or_1_out);
  not not_7 (not_7_out, and_3_out);
  LED NACT (.in(nor_2_out));
  LED DTB (.in(nor_3_out));
  LED DWS (.in(nor_4_out));
  LED INTAK (.in(and_4_out));
  and and_4 (and_4_out, or_1_out, and_3_out);
  // Probe on or_1_out
  // Probe on and_3_out
  // Probe on nWR_RD
  // Probe on not_3_out
  // Probe on nWR_RD

  // Notes on the sheet:
  //   CPU READ/WRITE
  //   PSG BUS STATE
endmodule
