// Logisim project A_Better_Solution.circ as structural Verilog: 1 circuit, main circuit main
module main (
  input  A0,
  input  nDEV_SEL,
  input  nWR_RD
);

  wire and_1_out, and_2_out, and_3_out, and_4_out, and_5_out, and_6_out, d_ff_1_q, d_ff_2_qn, d_ff_3_q,
       d_ff_4_q, nor_1_out, nor_2_out, nor_3_out, not_1_out, not_2_out, not_3_out, not_4_out, not_5_out,
       not_6_out, not_7_out, not_8_out, or_1_out, or_2_out, PHI2_out;

  Clock PHI2 (.out(PHI2_out));
  nor nor_1 (nor_1_out, and_6_out, or_2_out);
  not not_1 (not_1_out, PHI2_out);
  nor nor_2 (nor_2_out, and_6_out, not_2_out);
  nor nor_3 (nor_3_out, not_3_out, or_2_out);
  not not_2 (not_2_out, or_2_out);
  not not_3 (not_3_out, and_6_out);
  not not_4 (not_4_out, nWR_RD);
  and and_1 (and_1_out, or_2_out, and_6_out);
  and and_2 (and_2_out, PHI2_out, nWR_RD);
  and and_3 (and_3_out, not_4_out, not_1_out);
  LED NACT (.in(nor_1_out));
  LED DTB (.in(nor_2_out));
  LED DWS (.in(nor_3_out));
  LED INTAK (.in(and_1_out));
  or or_1 (or_1_out, and_2_out, and_3_out);
  not not_5 (not_5_out, nDEV_SEL);
  not not_6 (not_6_out, nWR_RD);
  LED READ (.in(nWR_RD));
  LED WRITE (.in(not_6_out));
  LED nDEVSEL (.in(not_5_out));
  LED ADDR0 (.in(A0));
  D_Flip_Flop d_ff_1 (.D(A0), .clk(or_1_out), .Q(d_ff_1_q), .reset(d_ff_4_q));  // open: Qn, preset
  D_Flip_Flop d_ff_2 (.D(nDEV_SEL), .clk(or_1_out), .Qn(d_ff_2_qn), .preset(d_ff_4_q));  // open: Q, reset
  D_Flip_Flop d_ff_3 (.D(nWR_RD), .clk(or_1_out), .Q(d_ff_3_q));  // open: Qn, preset, reset
  not not_7 (not_7_out, or_1_out);
  Button button_1 ();  // open: out
  D_Flip_Flop d_ff_4 (.D(d_ff_3_q), .clk(not_7_out), .Q(d_ff_4_q), .reset(d_ff_4_q));  // open: Qn, preset
  and and_4 (and_4_out, d_ff_1_q, d_ff_2_qn);
  and and_5 (and_5_out, d_ff_2_qn, d_ff_3_q);
  not not_8 (not_8_out, d_ff_3_q);
  or or_2 (or_2_out, and_4_out, and_5_out);
  and and_6 (and_6_out, d_ff_2_qn, not_8_out);

  // Notes on the sheet:
  //   PSG BUS STATE
endmodule
