// Logisim project solution_RW_indirect_addressing.circ as structural Verilog: 1 circuit, main circuit main
module main (
  input  nRD,
  input  nSEL,
  input  A0,
  output bdir,
  output bc1
);

  wire and_2_out, and_3_out, not_1_out, not_2_out;

  not not_1 (not_1_out, nRD);
  not not_2 (not_2_out, nSEL);
  and and_1 (bdir, not_2_out, nRD);
  and and_2 (and_2_out, not_2_out, not_1_out);
  and and_3 (and_3_out, A0, not_2_out);
  or or_1 (bc1, and_2_out, and_3_out);
endmodule
