// Logisim project ATmegaZ80.circ as structural Verilog: 1 circuit, main circuit main
module main (
  input  A7,
  input  A6,
  input  WS_DISABLE,
  input  A5,
  input  A4,
  input  A0,
  input  nM1,
  input  nIOREQ,
  input  nRD,
  input  nWR,
  input  in_11,
  input  in_12,
  input  D0,
  input  Z_INT_ISR0,
  input  D1,
  input  D2,
  input  D3,
  input  Z_INT_ISR1,
  input  D4,
  input  D5,
  input  D6,
  input  D7,
  input  Z80_nINT,
  input  ADD7,
  input  ADD6,
  input  ADD5,
  input  ADD4,
  input  ADD0,
  input  N_M1,
  input  N_IOREQ,
  input  N_RD,
  input  N_WR,
  input  Z80_INT0,
  input  Z80_INT1,
  input  in_35,
  input  in_36,
  input  in_37,
  input  in_38,
  input  in_39,
  input  in_40,
  input  in_41,
  input  in_42,
  input  in_43,
  input  in_44,
  input  in_45,
  input  in_46,
  input  in_47,
  input  in_48,
  input  in_49,
  input  in_50,
  input  in_51,
  input  in_52,
  input  in_53,
  input  in_54,
  input  in_55,
  input  in_56,
  output nWAIT,
  output nOE,
  output DIR,
  output INT1,
  output INT0,
  output TP_nOE,
  output INTR1,
  output INTR2,
  output TP_DIRAB
);

  wire and_1_out, and_2_out, and_3_out, and_4_out, and_5_out, and_6_out, and_7_out, and_8_out, d_ff_1_qn,
       d_ff_2_q, d_ff_2_qn, d_ff_3_q, d_ff_3_qn, d_ff_4_q, dipswitch_1_p1, dipswitch_1_p2, dipswitch_1_p3,
       dipswitch_1_p4, dipswitch_1_p5, dipswitch_1_p6, dipswitch_1_p7, dipswitch_1_p8, n7400_1_pin6,
       n7404_1_pin3, n7404_1_pin5, n7404_1_pin8, n7404_1_pin10, n7404_2_pin4, n7404_2_pin6, n7404_2_pin8,
       n7404_2_pin10, n7404_2_pin12, n7430_1_pin11, n7432_1_pin8, n7432_1_pin11, n7474_1_pin1, n7474_1_pin4,
       n7474_1_pin5, n7474_1_pin6, n7474_1_pin8, n7474_1_pin9, n7474_1_pin10, n7474_1_pin11, n7474_1_pin13,
       n74244_1_pin2, n74245_1_pin2, n74245_1_pin3, n74245_1_pin4, n74245_1_pin5, n74245_1_pin6,
       n74245_1_pin7, n74245_1_pin8, n74245_1_pin9, nand_1_out, nand_2_out, nand_3_out, nand_5_out,
       nand_6_out, nor_1_out, nor_2_out, not_1_out, not_2_out, not_3_out, not_4_out, not_5_out, not_6_out,
       not_7_out, not_8_out, not_9_out, not_10_out, not_11_out, not_12_out, not_13_out, or_1_out, or_2_out,
       or_3_out, or_4_out, or_5_out, or_6_out, or_7_out, or_8_out;

  not not_1 (not_1_out, in_44);
  // DipSwitch dipswitch_1: pin names not known; wires that end beside it: dipswitch_1_p1, dipswitch_1_p2, dipswitch_1_p3, dipswitch_1_p4, dipswitch_1_p5, dipswitch_1_p6, dipswitch_1_p7, dipswitch_1_p8, dipswitch_1_p1, dipswitch_1_p2, dipswitch_1_p3, dipswitch_1_p4, dipswitch_1_p5, dipswitch_1_p6, dipswitch_1_p7, dipswitch_1_p8
  _74245 #(.ShowInternalStructure("true")) u_74245_1 (
    .pin1(N_RD), .pin2(n74245_1_pin2), .pin3(n74245_1_pin3), .pin4(n74245_1_pin4), .pin5(n74245_1_pin5),
    .pin6(n74245_1_pin6), .pin7(n74245_1_pin7), .pin8(n74245_1_pin8), .pin9(n74245_1_pin9), .pin19(TP_nOE),
    .pin18(dipswitch_1_p8), .pin17(dipswitch_1_p7), .pin16(dipswitch_1_p6), .pin15(dipswitch_1_p5),
    .pin14(dipswitch_1_p4), .pin13(dipswitch_1_p3), .pin12(dipswitch_1_p2), .pin11(dipswitch_1_p1));
  and and_1 (and_1_out, in_35, in_36, in_37);
  and and_2 (and_2_out, in_39, in_40, in_41);
  and and_3 (and_3_out, in_42, in_43, not_1_out);
  not not_2 (not_2_out, in_43);
  not not_3 (not_3_out, not_2_out);
  not not_4 (not_4_out, in_43);
  not not_5 (not_5_out, in_44);
  nand nand_1 (nand_1_out, A7, A6);
  nand nand_2 (nand_2_out, A5, A4);
  nand nand_3 (nand_3_out, A0, nM1);
  not not_6 (not_6_out, and_5_out);
  not not_7 (not_7_out, nM1);
  not not_8 (not_8_out, nIOREQ);
  not not_9 (not_9_out, not_3_out);
  and and_4 (and_4_out, not_4_out, not_5_out);
  not not_10 (not_10_out, and_4_out);
  not not_11 (not_11_out, not_10_out);
  assign in_47 = not_11_out ? 1'b0 : 1'bz;  // Controlled_Buffer controlled_buffer_1
  assign in_49 = not_11_out ? or_2_out : 1'bz;  // Controlled_Buffer controlled_buffer_2
  assign in_50 = not_11_out ? or_3_out : 1'bz;  // Controlled_Buffer controlled_buffer_3
  assign in_51 = not_11_out ? 1'b1 : 1'bz;  // Controlled_Buffer controlled_buffer_4
  assign in_53 = not_11_out ? 1'b1 : 1'bz;  // Controlled_Buffer controlled_buffer_5
  assign in_54 = not_11_out ? 1'b1 : 1'bz;  // Controlled_Buffer controlled_buffer_6
  assign in_55 = not_11_out ? 1'b1 : 1'bz;  // Controlled_Buffer controlled_buffer_7
  assign in_56 = not_11_out ? 1'b1 : 1'bz;  // Controlled_Buffer controlled_buffer_8
  nor nor_1 (nor_1_out, nand_1_out, nand_2_out);
  nor nor_2 (nor_2_out, nand_3_out, nIOREQ);
  or or_1 (or_1_out, not_6_out, in_12);
  and and_5 (and_5_out, not_7_out, not_8_out);
  and and_6 (and_6_out, and_1_out, and_2_out, and_3_out);
  and and_7 (and_7_out, not_9_out, in_43);
  or or_2 (or_2_out, in_48, d_ff_3_qn);
  or or_3 (or_3_out, d_ff_3_qn, in_52);
  nand nand_4 (nOE, nor_1_out, nor_2_out);
  or or_4 (or_4_out, in_11, or_1_out);
  assign D0 = and_5_out ? 1'b0 : 1'bz;  // Controlled_Buffer controlled_buffer_9
  assign D1 = and_5_out ? or_5_out : 1'bz;  // Controlled_Buffer controlled_buffer_10
  assign D2 = and_5_out ? or_6_out : 1'bz;  // Controlled_Buffer controlled_buffer_11
  assign D3 = and_5_out ? 1'b1 : 1'bz;  // Controlled_Buffer controlled_buffer_12
  assign D4 = and_5_out ? 1'b1 : 1'bz;  // Controlled_Buffer controlled_buffer_13
  assign D5 = and_5_out ? 1'b1 : 1'bz;  // Controlled_Buffer controlled_buffer_14
  assign D6 = and_5_out ? 1'b1 : 1'bz;  // Controlled_Buffer controlled_buffer_15
  assign D7 = and_5_out ? 1'b1 : 1'bz;  // Controlled_Buffer controlled_buffer_16
  _7404 #(.ShowInternalStructure("true")) u_7404_1 (
    .pin3(n7404_1_pin3), .pin4(INTR1), .pin5(n7404_1_pin5), .pin6(INTR2), .pin11(TP_nOE),
    .pin10(n7404_1_pin10), .pin9(N_IOREQ), .pin8(n7404_1_pin8));  // open: pin1, pin2, pin13, pin12
  nand nand_5 (nand_5_out, in_48, in_52);
  D_Flip_Flop d_ff_1 (.D(1'b0), .clk(not_12_out), .Q(nWAIT), .Qn(d_ff_1_qn), .preset(WS_DISABLE), .reset(1'b0));
  not not_12 (not_12_out, nOE);
  and and_8 (and_8_out, or_4_out, and_5_out);
  or or_5 (or_5_out, Z_INT_ISR0, Z80_nINT);
  or or_6 (or_6_out, Z80_nINT, Z_INT_ISR1);
  D_Flip_Flop d_ff_2 (.D(1'b0), .clk(and_6_out), .Q(d_ff_2_q), .Qn(d_ff_2_qn), .preset(in_38), .reset(1'b0));
  D_Flip_Flop d_ff_3 (.D(1'b1), .clk(nand_5_out), .Q(d_ff_3_q), .Qn(d_ff_3_qn), .preset(1'b0), .reset(and_7_out));
  or or_7 (or_7_out, in_45, d_ff_2_q);
  or or_8 (or_8_out, d_ff_2_q, in_46);
  // NoConnect on d_ff_1_qn
  // NoConnect on d_ff_2_qn
  not not_13 (not_13_out, and_6_out);
  // NoConnect on d_ff_3_q
  // NoConnect on d_ff_4_q
  D_Flip_Flop d_ff_4 (.D(1'b1), .clk(nand_6_out), .Q(d_ff_4_q), .Qn(Z80_nINT), .preset(1'b0), .reset(and_8_out));
  nand nand_6 (nand_6_out, Z_INT_ISR0, Z_INT_ISR1);
  _7430 #(.ShowInternalStructure("true")) u_7430_1 (
    .pin1(N_M1), .pin2(ADD0), .pin3(ADD4), .pin4(ADD5), .pin5(ADD6), .pin6(ADD7), .pin12(n7404_1_pin8),
    .pin11(n7430_1_pin11), .pin8(TP_nOE));  // open: pin13, pin10, pin9
  nor nor_3 (INT1, nRD, nWAIT);
  nor nor_4 (INT0, nWAIT, nWR);
  _7474 #(.ShowInternalStructure("true")) u_7474_1 (
    .pin1(n7474_1_pin1), .pin2(n7474_1_pin1), .pin3(n7404_1_pin10), .pin4(n7474_1_pin4), .pin5(n7474_1_pin5),
    .pin6(n7474_1_pin6), .pin13(n7474_1_pin13), .pin12(n7474_1_pin1), .pin11(n7474_1_pin11),
    .pin10(n7474_1_pin10), .pin9(n7474_1_pin9), .pin8(n7474_1_pin8));
  // NoConnect on n7474_1_pin9
  // NoConnect on n7474_1_pin4
  _7432 #(.ShowInternalStructure("true")) u_7432_1 (
    .pin1(N_RD), .pin2(n7474_1_pin5), .pin3(n7404_1_pin5), .pin4(n7474_1_pin5), .pin5(N_WR),
    .pin6(n7404_1_pin3), .pin13(Z80_INT0), .pin12(n7474_1_pin8), .pin11(n7432_1_pin11), .pin10(Z80_INT1),
    .pin9(n7474_1_pin8), .pin8(n7432_1_pin8));
  _7404 #(.ShowInternalStructure("true")) u_7404_2 (
    .pin3(N_M1), .pin4(n7404_2_pin4), .pin5(N_IOREQ), .pin6(n7404_2_pin6), .pin13(N_M1),
    .pin12(n7404_2_pin12), .pin11(n7404_2_pin12), .pin10(n7404_2_pin10), .pin9(n7404_2_pin10),
    .pin8(n7404_2_pin8));  // open: pin1, pin2
  _7400 #(.ShowInternalStructure("true")) u_7400_1 (
    .pin4(n7404_2_pin6), .pin5(n7404_2_pin4), .pin6(n7400_1_pin6), .pin13(Z80_INT0), .pin12(Z80_INT1),
    .pin11(n7474_1_pin11), .pin10(n7404_2_pin8), .pin9(N_M1), .pin8(n7474_1_pin13));  // open: pin1, pin2, pin3
  _74244 #(.ShowInternalStructure("true")) u_74244_1 (
    .pin1(n7400_1_pin6), .pin2(n74244_1_pin2), .pin3(n74245_1_pin3), .pin4(n74244_1_pin2),
    .pin5(n74245_1_pin5), .pin6(n74244_1_pin2), .pin7(n74245_1_pin7), .pin8(n74244_1_pin2),
    .pin9(n74245_1_pin9), .pin19(n7400_1_pin6), .pin18(n74245_1_pin2), .pin17(n74244_1_pin2),
    .pin16(n74245_1_pin4), .pin15(n7432_1_pin8), .pin14(n74245_1_pin6), .pin13(n7432_1_pin11),
    .pin12(n74245_1_pin8), .pin11(n74244_1_pin2));

  assign DIR = nRD;
  assign TP_DIRAB = N_RD;
  // also tied to GND on the sheet: n7474_1_pin1
  // also tied to VCC on the sheet: {n7474_1_pin10, n7430_1_pin11, n74244_1_pin2}
endmodule
