// Logisim project IM2hardware.circ as structural Verilog: 1 circuit, main circuit main
module main (
  input  nM1,
  input  nIOREQ,
  input  in_3,
  input  nINT_ISR1,
  input  nINT_ISR0,
  input  ISR1,
  input  ISR0,
  input  M1,
  input  IOREQ,
  output nINT,
  output out_11,
  output out_12,
  output out_13,
  output out_14,
  output out_15,
  output out_16,
  output out_17,
  output out_18
);

  wire and_1_out, and_2_out, INT_Z80, n7400_1_pin6, n7400_1_pin8, n7404_1_pin1, n7404_1_pin2, n7404_1_pin4,
       n7404_1_pin6, n7404_1_pin10, n7404_1_pin12, n7432_1_pin8, n7432_1_pin11, n7474_1_pin12, n74245_1_pin1,
       n74245_1_pin18, nand_1_out, not_1_out, not_2_out, not_3_out, not_4_out, not_5_out, not_6_out,
       or_1_out, or_2_out;
  wire [3:0] n74245_1_pin5, n74245_1_pin9;

  _7404 #(.ShowInternalStructure("true")) u_7404_1 (
    .pin1(n7404_1_pin1), .pin2(n7404_1_pin2), .pin3(n7404_1_pin2), .pin4(n7404_1_pin4), .pin5(n7404_1_pin4),
    .pin6(n7404_1_pin6), .pin13(IOREQ), .pin12(n7404_1_pin12), .pin11(M1), .pin10(n7404_1_pin10));  // open: pin9, pin8
  D_Flip_Flop d_ff_1 (.D(1'b1), .clk(nand_1_out), .Qn(nINT), .preset(in_3), .reset(and_1_out));  // open: Q
  nand nand_1 (nand_1_out, nINT_ISR1, nINT_ISR0);
  _7400 #(.ShowInternalStructure("true")) u_7400_1 (
    .pin4(n7404_1_pin6), .pin5(n7404_1_pin1), .pin6(n7400_1_pin6), .pin13(n7404_1_pin12),
    .pin12(n7404_1_pin10), .pin11(n7404_1_pin1), .pin10(ISR0), .pin9(ISR1), .pin8(n7400_1_pin8));  // open: pin1, pin2, pin3
  and and_1 (and_1_out, not_4_out, not_1_out);
  not not_1 (not_1_out, not_2_out);
  or or_1 (or_1_out, nINT_ISR1, nINT);
  or or_2 (or_2_out, nINT, nINT_ISR0);
  _7474 #(.ShowInternalStructure("true")) u_7474_1 (
    .pin13(n7400_1_pin6), .pin12(n7474_1_pin12), .pin11(n7400_1_pin8), .pin10(n7474_1_pin12), .pin8(INT_Z80));  // open: pin1, pin2, pin3, pin4, pin5, pin6, pin9
  not not_2 (not_2_out, not_3_out);
  not not_3 (not_3_out, not_4_out);
  assign out_11 = and_2_out ? 1'b1 : 1'bz;  // Controlled_Buffer controlled_buffer_1
  assign out_12 = and_2_out ? 1'b1 : 1'bz;  // Controlled_Buffer controlled_buffer_2
  assign out_13 = and_2_out ? 1'b1 : 1'bz;  // Controlled_Buffer controlled_buffer_3
  assign out_14 = and_2_out ? 1'b1 : 1'bz;  // Controlled_Buffer controlled_buffer_4
  assign out_15 = and_2_out ? 1'b1 : 1'bz;  // Controlled_Buffer controlled_buffer_5
  assign out_16 = and_2_out ? or_1_out : 1'bz;  // Controlled_Buffer controlled_buffer_6
  assign out_17 = and_2_out ? or_2_out : 1'bz;  // Controlled_Buffer controlled_buffer_7
  assign out_18 = and_2_out ? 1'b0 : 1'bz;  // Controlled_Buffer controlled_buffer_8
  Hex_Digit_Display hex_digit_display_1 (.value(n74245_1_pin5));  // open: dp
  Hex_Digit_Display hex_digit_display_2 (.value(n74245_1_pin9));  // open: dp
  not not_4 (not_4_out, and_2_out);
  _7432 #(.ShowInternalStructure("true")) u_7432_1 (
    .pin13(INT_Z80), .pin12(ISR1), .pin11(n7432_1_pin11), .pin10(INT_Z80), .pin9(ISR0), .pin8(n7432_1_pin8));  // open: pin1, pin2, pin3, pin4, pin5, pin6
  not not_5 (not_5_out, nM1);
  and and_2 (and_2_out, not_5_out, not_6_out);
  not not_6 (not_6_out, nIOREQ);
  _74245 #(.ShowInternalStructure("true")) u_74245_1 (
    .pin1(n74245_1_pin1), .pin2(n74245_1_pin5[3]), .pin3(n74245_1_pin5[2]), .pin4(n74245_1_pin5[1]),
    .pin5(n74245_1_pin5[0]), .pin6(n74245_1_pin9[3]), .pin7(n74245_1_pin9[2]), .pin8(n74245_1_pin9[1]),
    .pin9(n74245_1_pin9[0]), .pin19(n7404_1_pin1), .pin18(n74245_1_pin18), .pin17(n74245_1_pin18),
    .pin16(n74245_1_pin18), .pin15(n74245_1_pin18), .pin14(n74245_1_pin18), .pin13(n7432_1_pin11),
    .pin12(n7432_1_pin8), .pin11(n74245_1_pin1));
  Hex_Digit_Display hex_digit_display_3 (.value({out_14, out_13, out_12, out_11}));  // open: dp
  Hex_Digit_Display hex_digit_display_4 (.value({out_15, out_16, out_17, out_18}));  // open: dp
  // also tied to GND on the sheet: n74245_1_pin1
  // also tied to VCC on the sheet: {n7474_1_pin12, n74245_1_pin18}

  // Notes on the sheet:
  //   ISR1: initial=0x1
  //   ISR0: initial=0x1
  //   M1: initial=0x1
  //   IOREQ: initial=0x1
  //   Home Computer Group : fb.com/groups/home.computer
  //   Home Computer Group : fb.com/groups/home.computer
  //   Distributed under Creative Common Attribution 4.0 International
  //   https://homecomputer.group/license
endmodule
